// Logisim project finalSAM.circ as structural Verilog: 1 circuit, main circuit main
module main (
  input  memclr,
  output [7:0] out_2,
  output SUB,
  output Inc,
  output Amux,
  output MAR,
  output Mst,
  output Ir,
  output Dmux,
  output Acc,
  output OUT
);

  wire and_1_out, and_2_out, and_3_out, clock_out, CLR_out, nor_1_out, not_1_out, or_1_out,
       priority_encoder_1_p2, priority_encoder_1_p3, priority_encoder_1_p4, priority_encoder_1_p5,
       priority_encoder_1_p6, priority_encoder_1_p7, priority_encoder_1_p8, priority_encoder_1_p9;
  wire [1:0] counter_1_q;
  wire [3:0] counter_2_q, Ir_q, Mar_q, multiplexer_1_out, not_2_out;
  wire [4:2] priority_encoder_1_p1;
  wire [7:0] Acc_q, adder_1_out, multiplexer_2_out, ram_1_data, xor_1_out;
  wire [7:4] Ir_q_2;
  wire [11:9] rom_1_data;

  or or_1 (or_1_out, rom_1_data[9], and_2_out);
  Button CLR (.out(CLR_out));
  and and_1 (and_1_out, not_1_out, clock_out);
  Counter #(.width(2), .max('h3)) counter_1 (
    .Q(counter_1_q), .clk(and_1_out), .clr(CLR_out));  // open: load, D, count, carry
  Counter #(.width(4), .max('hf)) counter_2 (
    .load(or_1_out), .D(Ir_q), .count(Inc), .Q(counter_2_q), .clk(and_1_out), .clr(CLR_out));  // open: carry
  not not_1 (not_1_out, rom_1_data[10]);
  Clock clock (.out(clock_out));
  nor nor_1 (nor_1_out, Acc_q[0], Acc_q[1], Acc_q[2], Acc_q[3], Acc_q[4], Acc_q[5], Acc_q[6], Acc_q[7]);
  Multiplexer #(.width(4), .enable("false")) multiplexer_1 (
    .in0(counter_2_q), .in1(Ir_q), .out(multiplexer_1_out), .sel(Amux));
  and and_2 (and_2_out, nor_1_out, rom_1_data[11]);
  Register #(.width(4)) u_Mar (.D(multiplexer_1_out), .en(MAR), .Q(Mar_q), .clk(and_1_out), .clr(CLR_out));
  and and_3 (and_3_out, memclr, CLR_out);
  ROM #(.addrWidth(5), .dataWidth(12)) rom_1 (
    .addr({priority_encoder_1_p1, counter_1_q}),
    .data({rom_1_data, Inc, Amux, MAR, Mst, Ir, Dmux, Acc, OUT, SUB}));  // open: sel
  RAM #(.addrWidth(4), .bus("separate")) ram_1 (
    .addr(Mar_q), .din(Acc_q), .data(ram_1_data), .str(Mst), .clk(and_1_out), .clr(and_3_out));  // open: sel, ld
  Multiplexer #(.width(8), .enable("false")) multiplexer_2 (
    .in0(adder_1_out), .in1(ram_1_data), .out(multiplexer_2_out), .sel(Dmux));
  Register u_Ir (.D(ram_1_data), .en(Ir), .Q({Ir_q_2, Ir_q}), .clk(and_1_out), .clr(CLR_out));
  Register u_Acc (.D(multiplexer_2_out), .en(Acc), .Q(Acc_q), .clk(and_1_out), .clr(CLR_out));
  Register u_Out (.D(Acc_q), .en(OUT), .Q(out_2), .clk(and_1_out));  // open: clr
  assign xor_1_out = ram_1_data ^ {8{SUB}};  // XOR_Gate xor_1, 8 bits wide
  // Priority_Encoder priority_encoder_1: pin names not known; wires that end beside it: priority_encoder_1_p1, priority_encoder_1_p2, priority_encoder_1_p3, priority_encoder_1_p4, priority_encoder_1_p5, priority_encoder_1_p6, priority_encoder_1_p7, priority_encoder_1_p8, priority_encoder_1_p9
  Adder adder_1 (.a(Acc_q), .b(xor_1_out), .out(adder_1_out), .cin(SUB));  // open: cout
  and LDA (priority_encoder_1_p2, not_2_out[3], not_2_out[2], not_2_out[1], not_2_out[0]);
  and Add (priority_encoder_1_p3, Ir_q_2[4], not_2_out[3], not_2_out[2], not_2_out[1]);
  and u_sub (priority_encoder_1_p4, Ir_q_2[5], not_2_out[3], not_2_out[2], not_2_out[0]);
  and sta (priority_encoder_1_p5, Ir_q_2[5], Ir_q_2[4], not_2_out[3], not_2_out[2]);
  and jmp (priority_encoder_1_p6, Ir_q_2[6], not_2_out[3], not_2_out[1], not_2_out[0]);
  and jaz (priority_encoder_1_p7, Ir_q_2[6], Ir_q_2[4], not_2_out[3], not_2_out[1]);
  and u_Out_2 (priority_encoder_1_p8, Ir_q_2[6], Ir_q_2[5], not_2_out[3], not_2_out[0]);
  and HLT (priority_encoder_1_p9, Ir_q_2[7], Ir_q_2[6], Ir_q_2[5], Ir_q_2[4]);
  assign not_2_out = ~Ir_q_2;  // NOT_Gate not_2, 4 bits wide

  // Notes on the sheet:
  //   contents of rom_1 (hex, n*v repeats v):
  //   140 10 c0 c 140 10 c0 4 140 10 c0 5 140 10 c0 20 140 10 200 0 140 10 800 0 140 10 2 0 140 10 400 400
endmodule
